// Digital circuit 3_input_decoder.dig as structural Verilog
module _3_input_decoder (
  input  y7,
  input  y6,
  input  y5,
  input  y4,
  input  y3,
  input  y2,
  input  y1,
  input  y0,
  output m_2,
  output m_1,
  output m_0
);

  wire and_1_out, and_2_out, and_3_out, and_4_out, and_5_out, and_6_out, xor_1_out, xor_2_out, xor_3_out,
       xor_4_out, xor_5_out, xor_6_out, xor_7_out, xor_8_out, xor_9_out, xor_10_out, xor_11_out, xor_12_out;

  xor xor_1 (xor_1_out, y7, y3);
  xor xor_2 (xor_2_out, y6, y2);
  xor xor_3 (xor_3_out, y5, y1);
  xor xor_4 (xor_4_out, y4, y0);
  xor xor_5 (xor_5_out, y7, y5);
  xor xor_6 (xor_6_out, y6, y4);
  xor xor_7 (xor_7_out, y3, y1);
  xor xor_8 (xor_8_out, y2, y0);
  xor xor_9 (xor_9_out, y7, y6);
  xor xor_10 (xor_10_out, y5, y4);
  xor xor_11 (xor_11_out, y3, y2);
  xor xor_12 (xor_12_out, y1, y0);
  and and_1 (and_1_out, xor_1_out, xor_3_out);
  and and_2 (and_2_out, xor_2_out, xor_4_out);
  and and_3 (and_3_out, xor_5_out, xor_7_out);
  and and_4 (and_4_out, xor_6_out, xor_8_out);
  and and_5 (and_5_out, xor_9_out, xor_11_out);
  and and_6 (and_6_out, xor_10_out, xor_12_out);
  or or_1 (m_2, and_1_out, and_2_out);
  or or_2 (m_1, and_3_out, and_4_out);
  or or_3 (m_0, and_5_out, and_6_out);
endmodule
