// Digital circuit 4bit_display.dig as structural Verilog
module _4bit_display (
  input  m_0,
  input  m_1,
  input  m_2,
  input  m_3
);

  wire not_1_out, not_2_out, not_3_out, not_4_out;

  Seven_Seg seven_seg_1 (
    .a(not_1_out), .b(1'b1), .c(1'b1), .d(not_1_out), .e(not_1_out), .f(not_1_out), .g(1'b0), .dp(1'b0));
  not not_1 (not_1_out, m_0);
  Seven_Seg seven_seg_2 (
    .a(not_2_out), .b(1'b1), .c(1'b1), .d(not_2_out), .e(not_2_out), .f(not_2_out), .g(1'b0), .dp(1'b0));
  not not_2 (not_2_out, m_1);
  not not_3 (not_3_out, m_2);
  Seven_Seg seven_seg_3 (
    .a(not_3_out), .b(1'b1), .c(1'b1), .d(not_3_out), .e(not_3_out), .f(not_3_out), .g(1'b0), .dp(1'b0));
  Seven_Seg seven_seg_4 (
    .a(not_4_out), .b(1'b1), .c(1'b1), .d(not_4_out), .e(not_4_out), .f(not_4_out), .g(1'b0), .dp(1'b0));
  not not_4 (not_4_out, m_3);
endmodule
