// Digital circuit 8Bit display.dig as structural Verilog
module _8Bit_display (
  input  y7,
  input  y6,
  input  y5,
  input  y4,
  input  y3,
  input  y2,
  input  y1,
  input  y0
);

  wire not_1_out, not_2_out, not_3_out, not_4_out, not_5_out, not_6_out, not_7_out, not_8_out;

  Seven_Seg seven_seg_1 (
    .a(not_1_out), .b(1'b1), .c(1'b1), .d(not_1_out), .e(not_1_out), .f(not_1_out), .g(1'b0), .dp(1'b0));
  not not_1 (not_1_out, y0);
  Seven_Seg seven_seg_2 (
    .a(not_2_out), .b(1'b1), .c(1'b1), .d(not_2_out), .e(not_2_out), .f(not_2_out), .g(1'b0), .dp(1'b0));
  not not_2 (not_2_out, y1);
  Seven_Seg seven_seg_3 (
    .a(not_3_out), .b(1'b1), .c(1'b1), .d(not_3_out), .e(not_3_out), .f(not_3_out), .g(1'b0), .dp(1'b0));
  not not_3 (not_3_out, y2);
  Seven_Seg seven_seg_4 (
    .a(not_4_out), .b(1'b1), .c(1'b1), .d(not_4_out), .e(not_4_out), .f(not_4_out), .g(1'b0), .dp(1'b0));
  not not_4 (not_4_out, y3);
  Seven_Seg seven_seg_5 (
    .a(not_5_out), .b(1'b1), .c(1'b1), .d(not_5_out), .e(not_5_out), .f(not_5_out), .g(1'b0), .dp(1'b0));
  not not_5 (not_5_out, y4);
  Seven_Seg seven_seg_6 (
    .a(not_6_out), .b(1'b1), .c(1'b1), .d(not_6_out), .e(not_6_out), .f(not_6_out), .g(1'b0), .dp(1'b0));
  not not_6 (not_6_out, y5);
  Seven_Seg seven_seg_7 (
    .a(not_7_out), .b(1'b1), .c(1'b1), .d(not_7_out), .e(not_7_out), .f(not_7_out), .g(1'b0), .dp(1'b0));
  not not_7 (not_7_out, y6);
  Seven_Seg seven_seg_8 (
    .a(not_8_out), .b(1'b1), .c(1'b1), .d(not_8_out), .e(not_8_out), .f(not_8_out), .g(1'b0), .dp(1'b0));
  not not_8 (not_8_out, y7);
endmodule
