// Digital circuit DecoderSimp.dig as structural Verilog
module DecoderSimp (
  input  y7,
  input  y6,
  input  y5,
  input  y4,
  input  y3,
  input  y2,
  input  y1,
  input  y0,
  output m0,
  output m1,
  output m2,
  output m3,
  output Valid,
  output Error2,
  output Error1
);

  wire and_1_out, and_2_out, and_3_out, and_4_out, and_5_out, and_6_out, and_7_out, and_8_out, and_9_out,
       and_10_out, and_11_out, and_12_out, and_14_out, and_15_out, FA1_c_o, FA1_s, FA2_c_o, FA2_s, FA3_c_o,
       FA3_s, FA4_c_o, FA4_s, FA5_c_o, FA5_s, FA6_c_o, FA6_s, FA7_c_o, FA7_s, Half_Adder1_c_o, Half_Adder1_s,
       Half_Adder2_c_o, Half_Adder2_s, Half_Adder3_c_o, Half_Adder3_s, Half_Adder4_c_o, Half_Adder4_s,
       not_1_out, not_2_out, not_3_out, not_4_out, not_5_out, not_6_out, not_7_out, not_8_out, xor_1_out,
       xor_2_out, xor_3_out, xor_4_out, xor_5_out, xor_6_out, xor_7_out, xor_8_out, xor_9_out, xor_10_out,
       xor_11_out, xor_12_out, xor_13_out, xor_14_out, xor_15_out, xor_16_out, xor_17_out, xor_18_out,
       xor_19_out, xor_20_out, xor_21_out, xor_22_out, xor_23_out, xor_24_out;

  xor xor_1 (xor_1_out, y7, y3);
  xor xor_2 (xor_2_out, y6, y2);
  xor xor_3 (xor_3_out, y5, y1);
  xor xor_4 (xor_4_out, y4, y0);
  xor xor_5 (xor_5_out, y7, y5);
  xor xor_6 (xor_6_out, y6, y4);
  xor xor_7 (xor_7_out, y3, y1);
  xor xor_8 (xor_8_out, y2, y0);
  xor xor_9 (xor_9_out, y7, y6);
  xor xor_10 (xor_10_out, y5, y4);
  xor xor_11 (xor_11_out, y3, y2);
  xor xor_12 (xor_12_out, y1, y0);
  and and_1 (and_1_out, xor_1_out, xor_3_out);
  and and_2 (and_2_out, xor_2_out, xor_4_out);
  and and_3 (and_3_out, xor_5_out, xor_7_out);
  and and_4 (and_4_out, xor_6_out, xor_8_out);
  and and_5 (and_5_out, xor_9_out, xor_11_out);
  and and_6 (and_6_out, xor_10_out, xor_12_out);
  or or_1 (m2, and_1_out, and_2_out);
  or or_2 (m1, and_3_out, and_4_out);
  or or_3 (m0, and_5_out, and_6_out);
  and and_7 (and_7_out, 1'b1, m0);
  xor xor_13 (xor_13_out, y7, and_7_out);
  xor xor_14 (xor_14_out, y5, and_7_out);
  xor xor_15 (xor_15_out, y3, and_7_out);
  xor xor_16 (xor_16_out, y1, and_7_out);
  and and_8 (and_8_out, 1'b1, m1);
  xor xor_17 (xor_17_out, xor_13_out, and_8_out);
  xor xor_18 (xor_18_out, y6, and_8_out);
  xor xor_19 (xor_19_out, xor_15_out, and_8_out);
  xor xor_20 (xor_20_out, y2, and_8_out);
  and and_9 (and_9_out, 1'b1, m2);
  xor xor_21 (xor_21_out, xor_17_out, and_9_out);
  xor xor_22 (xor_22_out, xor_18_out, and_9_out);
  xor xor_23 (xor_23_out, xor_14_out, and_9_out);
  xor xor_24 (xor_24_out, y4, and_9_out);
  Add Half_Adder1 (.a(xor_21_out), .b(1'b0), .c_i(xor_22_out), .s(Half_Adder1_s), .c_o(Half_Adder1_c_o));
  Add Half_Adder2 (.a(xor_23_out), .b(1'b0), .c_i(xor_24_out), .s(Half_Adder2_s), .c_o(Half_Adder2_c_o));
  Add Half_Adder3 (.a(xor_19_out), .b(1'b0), .c_i(xor_20_out), .s(Half_Adder3_s), .c_o(Half_Adder3_c_o));
  Add Half_Adder4 (.a(xor_16_out), .b(1'b0), .c_i(y0), .s(Half_Adder4_s), .c_o(Half_Adder4_c_o));
  Add FA1 (.a(Half_Adder1_s), .b(Half_Adder2_s), .c_i(1'b0), .s(FA1_s), .c_o(FA1_c_o));
  Add FA2 (.a(Half_Adder1_c_o), .b(Half_Adder2_c_o), .c_i(FA1_c_o), .s(FA2_s), .c_o(FA2_c_o));
  Add FA3 (.a(Half_Adder3_s), .b(Half_Adder4_s), .c_i(1'b0), .s(FA3_s), .c_o(FA3_c_o));
  Add FA4 (.a(Half_Adder3_c_o), .b(Half_Adder4_c_o), .c_i(FA3_c_o), .s(FA4_s), .c_o(FA4_c_o));
  Add FA5 (.a(FA1_s), .b(FA3_s), .c_i(1'b0), .s(FA5_s), .c_o(FA5_c_o));
  Add FA6 (.a(FA2_s), .b(FA4_s), .c_i(FA5_c_o), .s(FA6_s), .c_o(FA6_c_o));
  Add FA7 (.a(FA2_c_o), .b(FA4_c_o), .c_i(FA6_c_o), .s(FA7_s), .c_o(FA7_c_o));
  not not_1 (not_1_out, FA6_s);
  and and_10 (and_10_out, not_1_out, not_2_out);
  not not_2 (not_2_out, FA7_s);
  and and_11 (and_11_out, FA6_s, FA5_s);
  and and_12 (and_12_out, not_3_out, FA5_s);
  not not_3 (not_3_out, FA7_s);
  not not_4 (not_4_out, FA5_s);
  or or_4 (m3, FA7_s, FA7_c_o);
  not not_5 (not_5_out, FA7_c_o);
  not not_6 (not_6_out, FA7_c_o);
  and and_13 (Valid, not_4_out, and_10_out);
  and and_14 (and_14_out, not_5_out, and_11_out);
  and and_15 (and_15_out, not_6_out, and_12_out);
  or or_5 (Error1, and_14_out, and_15_out);
  and and_16 (Error2, not_7_out, not_8_out);
  not not_7 (not_7_out, Error1);
  not not_8 (not_8_out, Valid);

  // Notes on the sheet:
  //   m1: pin 1
  //   m2: pin 2
  //   m3: pin 3
  //   Based on Reed Decoder
  //   Half-Adder
  //   HA
  //   4-Bit
  //   Full-Adder
  //   3-Bit
  //   Full-Adder
endmodule
