// Digital circuit Full_Adder_1Bit.dig as structural Verilog
module Full_Adder_1Bit (
  input  a,
  input  b,
  input  cI,
  output s,
  output cO
);

  wire and_1_out, and_2_out, xor_1_out;

  and and_1 (and_1_out, a, b);
  xor xor_1 (xor_1_out, a, b);
  and and_2 (and_2_out, cI, xor_1_out);
  xor xor_2 (s, xor_1_out, cI);
  or or_1 (cO, and_1_out, and_2_out);
endmodule
