// Digital circuit Full_Adder_1Bit_CLA.dig as structural Verilog
// Cost: 2XOR + 1AND
module Full_Adder_1Bit_CLA (
  input  a,
  input  b,
  input  cI,
  output cO,
  output s
);

  wire xor_1_out;

  xor xor_1 (xor_1_out, a, b);
  and and_1 (cO, a, b);
  xor xor_2 (s, xor_1_out, cI);
endmodule
