// Digital circuit Full_Adder_4Bit.dig as structural Verilog
module Full_Adder_4Bit (
  input  a_0,
  input  b_0,
  input  a_1,
  input  a_1_2,
  output s_0,
  output s_1,
  output Co
);

  wire add_1_c_o;

  Add add_1 (.a(a_0), .b(b_0), .c_i(1'b0), .s(s_0), .c_o(add_1_c_o));
  Add add_2 (.a(a_1), .b(a_1_2), .c_i(add_1_c_o), .s(s_1), .c_o(Co));
endmodule
