// Digital circuit Full_Adder_4Bit_woci.dig as structural Verilog
module Full_Adder_4Bit_woci (
  input  a_0,
  input  b_0,
  input  a_1,
  input  b_1,
  output s_0,
  output s_1,
  output Co
);

  wire half_adder_1bit_1_co;

  Half_Adder_1Bit half_adder_1bit_1 (.a(a_0), .cI(b_0), .s(s_0), .cO(half_adder_1bit_1_co));
  Full_Adder_1Bit full_adder_1bit_1 (.a(a_1), .b(b_1), .cI(half_adder_1bit_1_co), .s(s_1), .cO(Co));
endmodule
