// Digital circuit Full_Adder_6Bit.dig as structural Verilog
module Full_Adder_6Bit (
  input  a_0,
  input  b_0,
  input  a_1,
  input  b_1,
  input  a_2,
  input  b_2,
  output s_0,
  output s_1,
  output s_2,
  output Co
);

  wire full_adder_1bit_1_co, half_adder_1bit_1_co;

  Half_Adder_1Bit half_adder_1bit_1 (.a(a_0), .cI(b_0), .s(s_0), .cO(half_adder_1bit_1_co));
  Full_Adder_1Bit full_adder_1bit_1 (.a(a_1), .b(b_1), .cI(half_adder_1bit_1_co), .s(s_1), .cO(full_adder_1bit_1_co));
  Full_Adder_1Bit_CLA full_adder_1bit_cla_1 (.a(a_2), .b(b_2), .cI(full_adder_1bit_1_co), .s(s_2), .cO(Co));

  // Notes on the sheet:
  //   Cost: 5XOR + 4AND + 1OR
endmodule
