// Digital circuit Mayority_voter.dig as structural Verilog
module Mayority_voter (
  input  m3_0,
  input  m3_1,
  input  m3_2,
  input  m3_3,
  input  m3_5,
  input  m3_4,
  input  m3_7,
  input  m3_6,
  output m3_d,
  output m3_c,
  output m3_b,
  output m3_a,
  output m0_3
);

  wire full_adder_4bit_woci_1_co, full_adder_4bit_woci_1_s_0, full_adder_4bit_woci_1_s_1,
       full_adder_4bit_woci_2_co, full_adder_4bit_woci_2_s_0, full_adder_4bit_woci_2_s_1,
       half_adder_1bit_1_co, half_adder_1bit_1_s, half_adder_1bit_2_co, half_adder_1bit_2_s,
       half_adder_1bit_3_co, half_adder_1bit_3_s, half_adder_1bit_4_co, half_adder_1bit_4_s;

  Half_Adder_1Bit half_adder_1bit_1 (.a(m3_7), .cI(m3_6), .s(half_adder_1bit_1_s), .cO(half_adder_1bit_1_co));
  Half_Adder_1Bit half_adder_1bit_2 (.a(m3_5), .cI(m3_4), .s(half_adder_1bit_2_s), .cO(half_adder_1bit_2_co));
  Half_Adder_1Bit half_adder_1bit_3 (.a(m3_3), .cI(m3_2), .s(half_adder_1bit_3_s), .cO(half_adder_1bit_3_co));
  Half_Adder_1Bit half_adder_1bit_4 (.a(m3_1), .cI(m3_0), .s(half_adder_1bit_4_s), .cO(half_adder_1bit_4_co));
  Full_Adder_4Bit_woci full_adder_4bit_woci_1 (
    .s_0(full_adder_4bit_woci_1_s_0), .s_1(full_adder_4bit_woci_1_s_1), .Co(full_adder_4bit_woci_1_co),
    .a_0(half_adder_1bit_1_s), .b_0(half_adder_1bit_2_s), .a_1(half_adder_1bit_1_co),
    .b_1(half_adder_1bit_2_co));
  Full_Adder_4Bit_woci full_adder_4bit_woci_2 (
    .s_0(full_adder_4bit_woci_2_s_0), .s_1(full_adder_4bit_woci_2_s_1), .Co(full_adder_4bit_woci_2_co),
    .a_0(half_adder_1bit_3_s), .b_0(half_adder_1bit_4_s), .a_1(half_adder_1bit_3_co),
    .b_1(half_adder_1bit_4_co));
  Full_Adder_6Bit full_adder_6bit_1 (
    .a_0(full_adder_4bit_woci_1_s_0), .b_0(full_adder_4bit_woci_2_s_0), .a_1(full_adder_4bit_woci_1_s_1),
    .b_1(full_adder_4bit_woci_2_s_1), .a_2(full_adder_4bit_woci_1_co), .b_2(full_adder_4bit_woci_2_co),
    .s_0(m3_d), .s_1(m3_c), .s_2(m3_b), .Co(m3_a));
  or or_1 (m0_3, m3_b, m3_a);

  // Notes on the sheet:
  //   m3_0: pin 1
  //   m3_1: pin 2
  //   m3_2: pin 3
  //   m3_3: pin 4
  //   m3_5: pin 6
  //   m3_4: pin 5
  //   m3_7: pin 8
  //   m3_6: pin 7
  //   m3_d: pin 13
  //   m3_c: pin 12
  //   m3_b: pin 11
  //   m3_a: pin 10
  //   m0_3: pin 9
  //   Half-Adder
  //   Total Cost: 5XOR gates + 1AND gate + 2OR gate
  //   HA
  //   8-Bit Population Counter
  //   2-Bit
  //   Full-Adder
  //   3-Bit
  //   Full-Adder
endmodule
