// Digital circuit Mo.dig as structural Verilog
module Mo (
  input  Hi,
  input  Gi,
  input  Fi,
  input  Di,
  input  Ci,
  input  Ei,
  input  Bi,
  input  Ai,
  output Mo
);

  wire and_1_out, and_2_out, xor_1_out, xor_2_out, xor_3_out, xor_4_out;

  xor xor_1 (xor_1_out, Hi, Gi);
  xor xor_2 (xor_2_out, Fi, Ei);
  xor xor_3 (xor_3_out, Di, Ci);
  xor xor_4 (xor_4_out, Bi, Ai);
  and and_1 (and_1_out, xor_1_out, xor_3_out);
  and and_2 (and_2_out, xor_2_out, xor_4_out);
  or or_1 (Mo, and_1_out, and_2_out);

  // Notes on the sheet:
  //   Hi: pin 8
  //   Gi: pin 7
  //   Fi: pin 6
  //   Di: pin 4
  //   Ci: pin 3
  //   Ei: pin 5
  //   Bi: pin 2
  //   Ai: pin 1
  //   Mo: pin 9
endmodule
