// Digital circuit ParEnc.dig as structural Verilog
module ParEnc (
  input  m4,
  input  m3,
  input  m2,
  input  m1,
  output x1,
  output x2,
  output x3,
  output x4,
  output x5,
  output x6,
  output x7,
  output x0
);

  wire xor_2_out, xor_3_out;

  xor xor_1 (x1, m4, m1);
  xor xor_2 (xor_2_out, m2, m1);
  xor xor_3 (xor_3_out, m2, m1);
  xor xor_4 (x2, m2, m4);
  xor xor_5 (x4, m4, m3);
  xor xor_6 (x3, xor_3_out, m4);
  xor xor_7 (x7, xor_2_out, x4);
  xor xor_8 (x6, m2, x4);
  xor xor_9 (x5, m1, x4);

  assign x0 = m4;
endmodule
