// Digital circuit ParEnc_0-7.dig as structural Verilog
module ParEnc_0_7 (
  input  m3,
  input  m2,
  input  m1,
  input  m0,
  output x1,
  output x2,
  output x3,
  output x4,
  output x5,
  output x6,
  output x7,
  output x0
);

  wire xor_1_out, xor_3_out;

  xor xor_1 (xor_1_out, m1, m0);
  xor xor_2 (x4, m2, m3);
  xor xor_3 (xor_3_out, m0, m1);
  xor xor_4 (x1, m3, m0);
  xor xor_5 (x2, m3, m1);
  xor xor_6 (x3, m3, xor_1_out);
  xor xor_7 (x5, x4, m0);
  xor xor_8 (x6, x4, m1);
  xor xor_9 (x7, x4, xor_3_out);

  assign x0 = m3;
endmodule
