// Digital circuit Par_Decoder_wo_outs.dig as structural Verilog
module Par_Decoder_wo_outs (
  input  y7,
  input  y6,
  input  y5,
  input  y4,
  input  y3,
  input  y2,
  input  y1,
  input  y0,
  output m0,
  output m1,
  output m2,
  output m3,
  output NoErrors,
  output E2,
  output E1
);

  wire mayority_voter_1_m3_a, mayority_voter_1_m3_b, mayority_voter_1_m3_c, mayority_voter_1_m3_d,
       reed_decoder_1_m3_0, reed_decoder_1_m3_1, reed_decoder_1_m3_2, reed_decoder_1_m3_3,
       reed_decoder_1_m3_4, reed_decoder_1_m3_5, reed_decoder_1_m3_6, reed_decoder_1_m3_7;

  _3_input_decoder _3_input_decoder_1 (
    .y7(y7), .y6(y6), .y5(y5), .y4(y4), .y3(y3), .y2(y2), .y1(y1), .y0(y0), .m0_2(m2), .m0_1(m1), .m0_0(m0));
  Reed_decoder reed_decoder_1 (
    .m3_7(reed_decoder_1_m3_7), .m3_6(reed_decoder_1_m3_6), .m3_5(reed_decoder_1_m3_5),
    .m3_4(reed_decoder_1_m3_4), .m3_3(reed_decoder_1_m3_3), .m3_2(reed_decoder_1_m3_2),
    .m3_1(reed_decoder_1_m3_1), .m3_0(reed_decoder_1_m3_0), .y7(y7), .y6(y6), .y5(y5), .y4(y4), .y3(y3),
    .y2(y2), .y1(y1), .y0(y0), .m0(m0), .m1(m1), .m2(m2));
  Mayority_voter mayority_voter_1 (
    .m3_7(reed_decoder_1_m3_7), .m3_6(reed_decoder_1_m3_6), .m3_5(reed_decoder_1_m3_5),
    .m3_4(reed_decoder_1_m3_4), .m3_3(reed_decoder_1_m3_3), .m3_2(reed_decoder_1_m3_2),
    .m3_1(reed_decoder_1_m3_1), .m3_0(reed_decoder_1_m3_0), .m3_d(mayority_voter_1_m3_d),
    .m3_c(mayority_voter_1_m3_c), .m3_b(mayority_voter_1_m3_b), .m3_a(mayority_voter_1_m3_a), .m0_3(m3));
  Validit_error_display validit_error_display_1 (
    .m3_c(mayority_voter_1_m3_c), .m3_d(mayority_voter_1_m3_d), .m3_b(mayority_voter_1_m3_b),
    .m3_a(mayority_voter_1_m3_a), ._1_Error(E1), ._2_Errors(E2), .Valid__No_Errors(NoErrors));
endmodule
