// Digital circuit Reed_decoder.dig as structural Verilog
module Reed_decoder (
  input  y7,
  input  y6,
  input  y5,
  input  y4,
  input  y3,
  input  y2,
  input  y1,
  input  y0,
  input  m2,
  input  m1,
  input  m0,
  output m3_7,
  output m3_6,
  output m3_5,
  output m3_4,
  output m3_3,
  output m3_2,
  output m3_1,
  output m3_0
);

  wire and_1_out, and_2_out, and_3_out, xor_1_out, xor_2_out, xor_3_out, xor_5_out, xor_6_out;

  and and_1 (and_1_out, 1'b1, m0);
  xor xor_1 (xor_1_out, y7, and_1_out);
  xor xor_2 (xor_2_out, y5, and_1_out);
  xor xor_3 (xor_3_out, y3, and_1_out);
  xor xor_4 (m3_1, y1, and_1_out);
  and and_2 (and_2_out, 1'b1, m1);
  xor xor_5 (xor_5_out, xor_1_out, and_2_out);
  xor xor_6 (xor_6_out, y6, and_2_out);
  xor xor_7 (m3_3, xor_3_out, and_2_out);
  xor xor_8 (m3_2, y2, and_2_out);
  and and_3 (and_3_out, 1'b1, m2);
  xor xor_9 (m3_7, xor_5_out, and_3_out);
  xor xor_10 (m3_6, xor_6_out, and_3_out);
  xor xor_11 (m3_5, xor_2_out, and_3_out);
  xor xor_12 (m3_4, y4, and_3_out);

  assign m3_0 = y0;
endmodule
