// Digital circuit Serial-Parallel_Encoder.dig as structural Verilog
module Serial_Parallel_Encoder (
  input  mi,
  input  clk,
  input  m0,
  input  m1,
  input  m2,
  input  m3,
  input  clk_2,
  input  LD,
  output Do,
  output Dox
);

  wire not_1_out, not_2_out, not_3_out, not_4_out, not_5_out, not_6_out, not_7_out, not_8_out, not_9_out,
       not_10_out, not_11_out, not_12_out, parenc_0_7_1_x0, parenc_0_7_1_x1, parenc_0_7_1_x2,
       parenc_0_7_1_x3, parenc_0_7_1_x4, parenc_0_7_1_x5, parenc_0_7_1_x6, parenc_0_7_1_x7;
  wire [3:0] serial_parallel_1_x0, serial_parallel_1_x4;

  not not_1 (not_1_out, m0);
  Seven_Seg seven_seg_1 (
    .a(not_1_out), .b(1'b1), .c(1'b1), .d(not_1_out), .e(not_1_out), .f(not_1_out), .g(1'b0), .dp(1'b0));
  not not_2 (not_2_out, m1);
  Seven_Seg seven_seg_2 (
    .a(not_2_out), .b(1'b1), .c(1'b1), .d(not_2_out), .e(not_2_out), .f(not_2_out), .g(1'b0), .dp(1'b0));
  not not_3 (not_3_out, m2);
  Seven_Seg seven_seg_3 (
    .a(not_3_out), .b(1'b1), .c(1'b1), .d(not_3_out), .e(not_3_out), .f(not_3_out), .g(1'b0), .dp(1'b0));
  not not_4 (not_4_out, m3);
  Seven_Seg seven_seg_4 (
    .a(not_4_out), .b(1'b1), .c(1'b1), .d(not_4_out), .e(not_4_out), .f(not_4_out), .g(1'b0), .dp(1'b0));
  _74165 _74165_1 (
    .pin1(LD), .pin2(clk_2), .pin3(1'b1), .pin4(1'b1), .pin5(1'b1), .pin6(1'b0), .pin7(Dox), .pin8(1'b0),
    .pin9(mi), .pin10(1'b0), .pin11(1'b0), .pin12(1'b0), .pin13(1'b0), .pin14(1'b0), .pin15(1'b0),
    .pin16(1'b1));
  // ScopeTrigger #(.trigger("rising")) scopetrigger_1: pin names not known; wires that end beside it: clk_2
  ParEnc_0_7 parenc_0_7_1 (
    .m0(m0), .m1(m1), .m2(m2), .m3(m3), .x0(parenc_0_7_1_x0), .x1(parenc_0_7_1_x1), .x2(parenc_0_7_1_x2),
    .x3(parenc_0_7_1_x3), .x4(parenc_0_7_1_x4), .x5(parenc_0_7_1_x5), .x6(parenc_0_7_1_x6),
    .x7(parenc_0_7_1_x7));
  Seven_Seg_Hex seven_seg_hex_1 (.d({m0, m1, m2, m3}), .dp(1'b0));
  Serial_parallel serial_parallel_1 (
    .mi(mi), .Clk(clk), .K0i(parenc_0_7_1_x0), .K1i(parenc_0_7_1_x1), .K2i(parenc_0_7_1_x2),
    .K3i(parenc_0_7_1_x3), .K4i(parenc_0_7_1_x4), .K5i(parenc_0_7_1_x5), .K6i(parenc_0_7_1_x6),
    .k7i(parenc_0_7_1_x7), .x0(serial_parallel_1_x0[0]), .x1(serial_parallel_1_x0[1]),
    .x2(serial_parallel_1_x0[2]), .x3(serial_parallel_1_x0[3]), .x4(serial_parallel_1_x4[0]),
    .x5(serial_parallel_1_x4[1]), .x6(serial_parallel_1_x4[2]), .x7(serial_parallel_1_x4[3]));
  Seven_Seg_Hex seven_seg_hex_2 (.d(serial_parallel_1_x0), .dp(1'b0));
  Seven_Seg_Hex seven_seg_hex_3 (.d(serial_parallel_1_x4), .dp(1'b0));
  Seven_Seg seven_seg_5 (
    .a(not_5_out), .b(1'b1), .c(1'b1), .d(not_5_out), .e(not_5_out), .f(not_5_out), .g(1'b0), .dp(1'b0));
  not not_5 (not_5_out, serial_parallel_1_x0[0]);
  Seven_Seg seven_seg_6 (
    .a(not_6_out), .b(1'b1), .c(1'b1), .d(not_6_out), .e(not_6_out), .f(not_6_out), .g(1'b0), .dp(1'b0));
  not not_6 (not_6_out, serial_parallel_1_x0[1]);
  Seven_Seg seven_seg_7 (
    .a(not_7_out), .b(1'b1), .c(1'b1), .d(not_7_out), .e(not_7_out), .f(not_7_out), .g(1'b0), .dp(1'b0));
  not not_7 (not_7_out, serial_parallel_1_x0[2]);
  Seven_Seg seven_seg_8 (
    .a(not_8_out), .b(1'b1), .c(1'b1), .d(not_8_out), .e(not_8_out), .f(not_8_out), .g(1'b0), .dp(1'b0));
  not not_8 (not_8_out, serial_parallel_1_x0[3]);
  Seven_Seg seven_seg_9 (
    .a(not_9_out), .b(1'b1), .c(1'b1), .d(not_9_out), .e(not_9_out), .f(not_9_out), .g(1'b0), .dp(1'b0));
  not not_9 (not_9_out, serial_parallel_1_x4[0]);
  Seven_Seg seven_seg_10 (
    .a(not_10_out), .b(1'b1), .c(1'b1), .d(not_10_out), .e(not_10_out), .f(not_10_out), .g(1'b0), .dp(1'b0));
  not not_10 (not_10_out, serial_parallel_1_x4[1]);
  Seven_Seg seven_seg_11 (
    .a(not_11_out), .b(1'b1), .c(1'b1), .d(not_11_out), .e(not_11_out), .f(not_11_out), .g(1'b0), .dp(1'b0));
  not not_11 (not_11_out, serial_parallel_1_x4[2]);
  Seven_Seg seven_seg_12 (
    .a(not_12_out), .b(1'b1), .c(1'b1), .d(not_12_out), .e(not_12_out), .f(not_12_out), .g(1'b0), .dp(1'b0));
  not not_12 (not_12_out, serial_parallel_1_x4[3]);

  assign Do = mi;

  // Notes on the sheet:
  //   mi: default 1
  //   clk: Hz: 2
  //   m3: default 1
  //   clk_2: Hz: 8
  //   m'0
  //   m'1
  //   m'2
  //   m'3
endmodule
