// Digital circuit Validit_error_display.dig as structural Verilog
module Validit_error_display (
  input  m3_d,
  input  m3_c,
  input  m3_b,
  input  m3_a,
  output _2_Errors,
  output _1_Error,
  output Valid__No_Errors
);

  wire and_1_out, and_2_out, and_3_out, and_4_out, and_5_out;

  and and_1 (and_1_out, m3_c, m3_d);
  and and_2 (and_2_out, ~m3_b, m3_d);  // And
  and and_3 (and_3_out, ~m3_c, ~m3_b);  // And
  and and_4 (and_4_out, ~m3_a, and_1_out);  // And
  and and_5 (and_5_out, ~m3_a, and_2_out);  // And
  and and_6 (Valid__No_Errors, ~m3_d, and_3_out);  // And
  or or_1 (_1_Error, and_4_out, and_5_out);
  and and_7 (_2_Errors, ~_1_Error, ~Valid__No_Errors);  // And
endmodule
