// Digital circuit Mayority_voter.dig as structural Verilog
module Mayority_voter (
  input  m_30,
  input  m_31,
  input  m_32,
  input  m_33,
  input  m_35,
  input  m_34,
  input  m_37,
  input  m_36,
  output m_3d,
  output m_3c,
  output m_3b,
  output m_3a
);

  wire add_1_c_o, add_1_s, add_2_c_o, add_2_s, add_3_c_o, add_3_s, add_4_c_o, add_4_s, add_5_c_o, add_5_s,
       add_6_c_o, add_6_s, add_7_c_o, add_7_s, add_8_c_o, add_8_s, add_9_c_o, add_10_c_o;

  Add add_1 (.a(m_37), .b(1'b0), .c_i(m_36), .s(add_1_s), .c_o(add_1_c_o));
  Add add_2 (.a(m_35), .b(1'b0), .c_i(m_34), .s(add_2_s), .c_o(add_2_c_o));
  Add add_3 (.a(m_33), .b(1'b0), .c_i(m_32), .s(add_3_s), .c_o(add_3_c_o));
  Add add_4 (.a(m_31), .b(1'b0), .c_i(m_30), .s(add_4_s), .c_o(add_4_c_o));
  Add add_5 (.a(add_1_s), .b(add_2_s), .c_i(1'b0), .s(add_5_s), .c_o(add_5_c_o));
  Add add_6 (.a(add_1_c_o), .b(add_2_c_o), .c_i(add_5_c_o), .s(add_6_s), .c_o(add_6_c_o));
  Add add_7 (.a(add_3_s), .b(add_4_s), .c_i(1'b0), .s(add_7_s), .c_o(add_7_c_o));
  Add add_8 (.a(add_3_c_o), .b(add_4_c_o), .c_i(add_7_c_o), .s(add_8_s), .c_o(add_8_c_o));
  Add add_9 (.a(add_5_s), .b(add_7_s), .c_i(1'b0), .s(m_3d), .c_o(add_9_c_o));
  Add add_10 (.a(add_6_s), .b(add_8_s), .c_i(add_9_c_o), .s(m_3c), .c_o(add_10_c_o));
  Add add_11 (.a(add_6_c_o), .b(add_8_c_o), .c_i(add_10_c_o), .s(m_3b), .c_o(m_3a));

  // Notes on the sheet:
  //   Half-Adder
  //   HA
  //   4-Bit
  //   Full-Adder
  //   3-Bit
  //   Full-Adder
endmodule
