// Digital circuit Reed_decoder.dig as structural Verilog
module Reed_decoder (
  input  y7,
  input  y6,
  input  y5,
  input  y4,
  input  y3,
  input  y2,
  input  y1,
  input  y0,
  input  m_2,
  input  m_1,
  input  m_0,
  output m_37,
  output m_36,
  output m_35,
  output m_34,
  output m_33,
  output m_32,
  output m_31,
  output m_30
);

  wire and_1_out, and_2_out, and_3_out, xor_1_out, xor_2_out, xor_3_out, xor_5_out, xor_6_out;

  and and_1 (and_1_out, 1'b1, m_0);
  xor xor_1 (xor_1_out, y7, and_1_out);
  xor xor_2 (xor_2_out, y5, and_1_out);
  xor xor_3 (xor_3_out, y3, and_1_out);
  xor xor_4 (m_31, y1, and_1_out);
  and and_2 (and_2_out, 1'b1, m_1);
  xor xor_5 (xor_5_out, xor_1_out, and_2_out);
  xor xor_6 (xor_6_out, y6, and_2_out);
  xor xor_7 (m_33, xor_3_out, and_2_out);
  xor xor_8 (m_32, y2, and_2_out);
  and and_3 (and_3_out, 1'b1, m_2);
  xor xor_9 (m_37, xor_5_out, and_3_out);
  xor xor_10 (m_36, xor_6_out, and_3_out);
  xor xor_11 (m_35, xor_2_out, and_3_out);
  xor xor_12 (m_34, y4, and_3_out);

  assign m_30 = y0;
endmodule
