// Digital circuit 3_input_decoder.dig as structural Verilog
module _3_input_decoder (
  input  y7,
  input  y6,
  input  y5,
  input  y4,
  input  y3,
  input  y2,
  input  y1,
  input  y0,
  output m0_2,
  output m0_1,
  output m0_0
);

  Mo mo_1 (.Hi(y7), .Gi(y3), .Fi(y6), .Ei(y2), .Di(y5), .Ci(y1), .Bi(y4), .Ai(y0), .Mo(m0_2));
  Mo mo_2 (.Hi(y7), .Gi(y5), .Fi(y6), .Ei(y4), .Di(y3), .Ci(y1), .Bi(y2), .Ai(y0), .Mo(m0_1));
  Mo mo_3 (.Hi(y7), .Gi(y6), .Fi(y5), .Ei(y4), .Di(y3), .Ci(y2), .Bi(y1), .Ai(y0), .Mo(m0_0));
endmodule
