// Digital circuit Decoder.dig as structural Verilog
module Decoder (
  input  y7,
  input  y6,
  input  y5,
  input  y4,
  input  y3,
  input  y2,
  input  y1,
  input  y0
);

  wire add_1_c_o, add_1_s, add_2_c_o, add_2_s, add_3_c_o, add_3_s, add_4_c_o, add_4_s, add_5_c_o, add_5_s,
       add_6_c_o, add_6_s, add_7_c_o, add_7_s, add_8_c_o, add_8_s, add_9_c_o, add_9_s, add_10_c_o, add_10_s,
       add_11_c_o, add_11_s, and_1_out, and_2_out, and_3_out, and_4_out, and_5_out, and_6_out, and_7_out,
       and_8_out, and_9_out, and_10_out, and_11_out, and_12_out, and_13_out, and_14_out, and_15_out,
       and_16_out, not_1_out, not_2_out, not_3_out, not_4_out, not_5_out, not_6_out, not_7_out, not_8_out,
       not_9_out, not_10_out, not_11_out, not_12_out, not_13_out, not_14_out, not_15_out, not_16_out,
       not_17_out, not_18_out, not_19_out, not_20_out, or_1_out, or_2_out, or_3_out, or_4_out, or_5_out,
       xor_1_out, xor_2_out, xor_3_out, xor_4_out, xor_5_out, xor_6_out, xor_7_out, xor_8_out, xor_9_out,
       xor_10_out, xor_11_out, xor_12_out, xor_13_out, xor_14_out, xor_15_out, xor_16_out, xor_17_out,
       xor_18_out, xor_19_out, xor_20_out, xor_21_out, xor_22_out, xor_23_out, xor_24_out;

  Seven_Seg seven_seg_1 (
    .a(not_1_out), .b(1'b1), .c(1'b1), .d(not_1_out), .e(not_1_out), .f(not_1_out), .g(1'b0), .dp(1'b0));
  not not_1 (not_1_out, y0);
  Seven_Seg seven_seg_2 (
    .a(not_2_out), .b(1'b1), .c(1'b1), .d(not_2_out), .e(not_2_out), .f(not_2_out), .g(1'b0), .dp(1'b0));
  not not_2 (not_2_out, y1);
  Seven_Seg seven_seg_3 (
    .a(not_3_out), .b(1'b1), .c(1'b1), .d(not_3_out), .e(not_3_out), .f(not_3_out), .g(1'b0), .dp(1'b0));
  not not_3 (not_3_out, y2);
  Seven_Seg seven_seg_4 (
    .a(not_4_out), .b(1'b1), .c(1'b1), .d(not_4_out), .e(not_4_out), .f(not_4_out), .g(1'b0), .dp(1'b0));
  not not_4 (not_4_out, y3);
  Seven_Seg seven_seg_5 (
    .a(not_5_out), .b(1'b1), .c(1'b1), .d(not_5_out), .e(not_5_out), .f(not_5_out), .g(1'b0), .dp(1'b0));
  not not_5 (not_5_out, y4);
  xor xor_1 (xor_1_out, y7, y3);
  xor xor_2 (xor_2_out, y6, y2);
  xor xor_3 (xor_3_out, y5, y1);
  xor xor_4 (xor_4_out, y4, y0);
  xor xor_5 (xor_5_out, y7, y5);
  xor xor_6 (xor_6_out, y6, y4);
  xor xor_7 (xor_7_out, y3, y1);
  xor xor_8 (xor_8_out, y2, y0);
  xor xor_9 (xor_9_out, y7, y6);
  xor xor_10 (xor_10_out, y5, y4);
  xor xor_11 (xor_11_out, y3, y2);
  xor xor_12 (xor_12_out, y1, y0);
  Seven_Seg seven_seg_6 (
    .a(not_6_out), .b(1'b1), .c(1'b1), .d(not_6_out), .e(not_6_out), .f(not_6_out), .g(1'b0), .dp(1'b0));
  not not_6 (not_6_out, y5);
  Seven_Seg seven_seg_7 (
    .a(not_7_out), .b(1'b1), .c(1'b1), .d(not_7_out), .e(not_7_out), .f(not_7_out), .g(1'b0), .dp(1'b0));
  not not_7 (not_7_out, y6);
  and and_1 (and_1_out, xor_1_out, xor_3_out);
  and and_2 (and_2_out, xor_2_out, xor_4_out);
  and and_3 (and_3_out, xor_5_out, xor_7_out);
  and and_4 (and_4_out, xor_6_out, xor_8_out);
  and and_5 (and_5_out, xor_9_out, xor_11_out);
  and and_6 (and_6_out, xor_10_out, xor_12_out);
  Seven_Seg seven_seg_8 (
    .a(not_8_out), .b(1'b1), .c(1'b1), .d(not_8_out), .e(not_8_out), .f(not_8_out), .g(1'b0), .dp(1'b0));
  not not_8 (not_8_out, y7);
  or or_1 (or_1_out, and_1_out, and_2_out);
  or or_2 (or_2_out, and_3_out, and_4_out);
  or or_3 (or_3_out, and_5_out, and_6_out);
  and and_7 (and_7_out, 1'b1, or_3_out);
  xor xor_13 (xor_13_out, y7, and_7_out);
  xor xor_14 (xor_14_out, y5, and_7_out);
  xor xor_15 (xor_15_out, y3, and_7_out);
  xor xor_16 (xor_16_out, y1, and_7_out);
  and and_8 (and_8_out, 1'b1, or_2_out);
  xor xor_17 (xor_17_out, xor_13_out, and_8_out);
  xor xor_18 (xor_18_out, y6, and_8_out);
  xor xor_19 (xor_19_out, xor_15_out, and_8_out);
  xor xor_20 (xor_20_out, y2, and_8_out);
  and and_9 (and_9_out, 1'b1, or_1_out);
  xor xor_21 (xor_21_out, xor_17_out, and_9_out);
  xor xor_22 (xor_22_out, xor_18_out, and_9_out);
  xor xor_23 (xor_23_out, xor_14_out, and_9_out);
  xor xor_24 (xor_24_out, y4, and_9_out);
  Add add_1 (.a(xor_21_out), .b(1'b0), .c_i(xor_22_out), .s(add_1_s), .c_o(add_1_c_o));
  Add add_2 (.a(xor_23_out), .b(1'b0), .c_i(xor_24_out), .s(add_2_s), .c_o(add_2_c_o));
  Add add_3 (.a(xor_19_out), .b(1'b0), .c_i(xor_20_out), .s(add_3_s), .c_o(add_3_c_o));
  Add add_4 (.a(xor_16_out), .b(1'b0), .c_i(y0), .s(add_4_s), .c_o(add_4_c_o));
  Add add_5 (.a(add_1_s), .b(add_2_s), .c_i(1'b0), .s(add_5_s), .c_o(add_5_c_o));
  Add add_6 (.a(add_1_c_o), .b(add_2_c_o), .c_i(add_5_c_o), .s(add_6_s), .c_o(add_6_c_o));
  Add add_7 (.a(add_3_s), .b(add_4_s), .c_i(1'b0), .s(add_7_s), .c_o(add_7_c_o));
  Add add_8 (.a(add_3_c_o), .b(add_4_c_o), .c_i(add_7_c_o), .s(add_8_s), .c_o(add_8_c_o));
  Add add_9 (.a(add_5_s), .b(add_7_s), .c_i(1'b0), .s(add_9_s), .c_o(add_9_c_o));
  Add add_10 (.a(add_6_s), .b(add_8_s), .c_i(add_9_c_o), .s(add_10_s), .c_o(add_10_c_o));
  Add add_11 (.a(add_6_c_o), .b(add_8_c_o), .c_i(add_10_c_o), .s(add_11_s), .c_o(add_11_c_o));
  not not_9 (not_9_out, add_10_s);
  and and_10 (and_10_out, not_9_out, not_10_out);
  not not_10 (not_10_out, add_11_s);
  and and_11 (and_11_out, add_10_s, add_9_s);
  and and_12 (and_12_out, not_11_out, add_9_s);
  not not_11 (not_11_out, add_11_s);
  not not_12 (not_12_out, add_9_s);
  or or_4 (or_4_out, add_11_s, add_11_c_o);
  not not_13 (not_13_out, add_11_c_o);
  not not_14 (not_14_out, add_11_c_o);
  and and_13 (and_13_out, not_12_out, and_10_out);
  and and_14 (and_14_out, not_13_out, and_11_out);
  and and_15 (and_15_out, not_14_out, and_12_out);
  LED Valid__No_Errors (.in(and_13_out));
  or or_5 (or_5_out, and_14_out, and_15_out);
  not not_15 (not_15_out, or_3_out);
  Seven_Seg seven_seg_9 (
    .a(not_15_out), .b(1'b1), .c(1'b1), .d(not_15_out), .e(not_15_out), .f(not_15_out), .g(1'b0), .dp(1'b0));
  Seven_Seg seven_seg_10 (
    .a(not_18_out), .b(1'b1), .c(1'b1), .d(not_18_out), .e(not_18_out), .f(not_18_out), .g(1'b0), .dp(1'b0));
  LED _1_Error (.in(or_5_out));
  and and_16 (and_16_out, not_16_out, not_17_out);
  not not_16 (not_16_out, or_5_out);
  not not_17 (not_17_out, and_13_out);
  not not_18 (not_18_out, or_2_out);
  Seven_Seg seven_seg_11 (
    .a(not_19_out), .b(1'b1), .c(1'b1), .d(not_19_out), .e(not_19_out), .f(not_19_out), .g(1'b0), .dp(1'b0));
  LED _2_Errors (.in(and_16_out));
  not not_19 (not_19_out, or_1_out);
  Seven_Seg seven_seg_12 (
    .a(not_20_out), .b(1'b1), .c(1'b1), .d(not_20_out), .e(not_20_out), .f(not_20_out), .g(1'b0), .dp(1'b0));
  not not_20 (not_20_out, or_4_out);

  // Notes on the sheet:
  //   Based on Reed Decoder
  //   Half-Adder
  //   HA
  //   4-Bit
  //   Full-Adder
  //   3-Bit
  //   Full-Adder
  //   m'0
  //   m'1
  //   m'2
  //   m'3
endmodule
