// Digital circuit Par_Decoder.dig as structural Verilog
module Par_Decoder (
  input  y7,
  input  y6,
  input  y5,
  input  y4,
  input  y3,
  input  y2,
  input  y1,
  input  y0
);

  wire _3_input_decoder_1_m0_0, _3_input_decoder_1_m0_1, _3_input_decoder_1_m0_2, Mayority_Vote_Counter_m0_3,
       Mayority_Vote_Counter_m3_a, Mayority_Vote_Counter_m3_b, Mayority_Vote_Counter_m3_c,
       Mayority_Vote_Counter_m3_d, not_1_out, not_2_out, not_3_out, not_4_out, not_5_out, not_6_out,
       not_7_out, not_8_out, not_9_out, not_10_out, not_11_out, not_12_out, Reed_Decoder_m_30,
       Reed_Decoder_m_31, Reed_Decoder_m_32, Reed_Decoder_m_33, Reed_Decoder_m_34, Reed_Decoder_m_35,
       Reed_Decoder_m_36, Reed_Decoder_m_37, validit_error_display_1__1_error,
       validit_error_display_1__2_errors, validit_error_display_1_valid__no_errors;

  Seven_Seg seven_seg_1 (
    .a(not_1_out), .b(1'b1), .c(1'b1), .d(not_1_out), .e(not_1_out), .f(not_1_out), .g(1'b0), .dp(1'b0));
  not not_1 (not_1_out, y0);
  Seven_Seg seven_seg_2 (
    .a(not_2_out), .b(1'b1), .c(1'b1), .d(not_2_out), .e(not_2_out), .f(not_2_out), .g(1'b0), .dp(1'b0));
  not not_2 (not_2_out, y1);
  Seven_Seg seven_seg_3 (
    .a(not_3_out), .b(1'b1), .c(1'b1), .d(not_3_out), .e(not_3_out), .f(not_3_out), .g(1'b0), .dp(1'b0));
  not not_3 (not_3_out, y2);
  Seven_Seg seven_seg_4 (
    .a(not_4_out), .b(1'b1), .c(1'b1), .d(not_4_out), .e(not_4_out), .f(not_4_out), .g(1'b0), .dp(1'b0));
  not not_4 (not_4_out, y3);
  Seven_Seg seven_seg_5 (
    .a(not_5_out), .b(1'b1), .c(1'b1), .d(not_5_out), .e(not_5_out), .f(not_5_out), .g(1'b0), .dp(1'b0));
  not not_5 (not_5_out, y4);
  Seven_Seg seven_seg_6 (
    .a(not_6_out), .b(1'b1), .c(1'b1), .d(not_6_out), .e(not_6_out), .f(not_6_out), .g(1'b0), .dp(1'b0));
  not not_6 (not_6_out, y5);
  Seven_Seg seven_seg_7 (
    .a(not_7_out), .b(1'b1), .c(1'b1), .d(not_7_out), .e(not_7_out), .f(not_7_out), .g(1'b0), .dp(1'b0));
  not not_7 (not_7_out, y6);
  Seven_Seg seven_seg_8 (
    .a(not_8_out), .b(1'b1), .c(1'b1), .d(not_8_out), .e(not_8_out), .f(not_8_out), .g(1'b0), .dp(1'b0));
  not not_8 (not_8_out, y7);
  _3_input_decoder _3_input_decoder_1 (
    .y7(y7), .y6(y6), .y5(y5), .y4(y4), .y3(y3), .y2(y2), .y1(y1), .y0(y0), .m0_2(_3_input_decoder_1_m0_2),
    .m0_1(_3_input_decoder_1_m0_1), .m0_0(_3_input_decoder_1_m0_0));
  Reed_decoder Reed_Decoder (
    .m_37(Reed_Decoder_m_37), .m_36(Reed_Decoder_m_36), .m_35(Reed_Decoder_m_35), .m_34(Reed_Decoder_m_34),
    .m_33(Reed_Decoder_m_33), .m_32(Reed_Decoder_m_32), .m_31(Reed_Decoder_m_31), .m_30(Reed_Decoder_m_30),
    .y7(y7), .y6(y6), .y5(y5), .y4(y4), .y3(y3), .y2(y2), .y1(y1), .y0(y0), .m_0(_3_input_decoder_1_m0_0),
    .m_1(_3_input_decoder_1_m0_1), .m_2(_3_input_decoder_1_m0_2));
  Mayority_voter Mayority_Vote_Counter (
    .m3_7(Reed_Decoder_m_37), .m3_6(Reed_Decoder_m_36), .m3_5(Reed_Decoder_m_35), .m3_4(Reed_Decoder_m_34),
    .m3_3(Reed_Decoder_m_33), .m3_2(Reed_Decoder_m_32), .m3_1(Reed_Decoder_m_31), .m3_0(Reed_Decoder_m_30),
    .m3_d(Mayority_Vote_Counter_m3_d), .m3_c(Mayority_Vote_Counter_m3_c), .m3_b(Mayority_Vote_Counter_m3_b),
    .m3_a(Mayority_Vote_Counter_m3_a), .m0_3(Mayority_Vote_Counter_m0_3));
  not not_9 (not_9_out, _3_input_decoder_1_m0_0);
  Seven_Seg seven_seg_9 (
    .a(not_9_out), .b(1'b1), .c(1'b1), .d(not_9_out), .e(not_9_out), .f(not_9_out), .g(1'b0), .dp(1'b0));
  not not_10 (not_10_out, _3_input_decoder_1_m0_1);
  Seven_Seg seven_seg_10 (
    .a(not_10_out), .b(1'b1), .c(1'b1), .d(not_10_out), .e(not_10_out), .f(not_10_out), .g(1'b0), .dp(1'b0));
  Validit_error_display validit_error_display_1 (
    .m3_c(Mayority_Vote_Counter_m3_c), .m3_d(Mayority_Vote_Counter_m3_d), .m3_b(Mayority_Vote_Counter_m3_b),
    .m3_a(Mayority_Vote_Counter_m3_a), ._1_Error(validit_error_display_1__1_error),
    ._2_Errors(validit_error_display_1__2_errors), .Valid__No_Errors(validit_error_display_1_valid__no_errors));
  not not_11 (not_11_out, _3_input_decoder_1_m0_2);
  Seven_Seg seven_seg_11 (
    .a(not_11_out), .b(1'b1), .c(1'b1), .d(not_11_out), .e(not_11_out), .f(not_11_out), .g(1'b0), .dp(1'b0));
  not not_12 (not_12_out, Mayority_Vote_Counter_m0_3);
  Seven_Seg seven_seg_12 (
    .a(not_12_out), .b(1'b1), .c(1'b1), .d(not_12_out), .e(not_12_out), .f(not_12_out), .g(1'b0), .dp(1'b0));
  LED led_1 (.in(validit_error_display_1__1_error));
  LED led_2 (.in(validit_error_display_1__2_errors));
  LED led_3 (.in(validit_error_display_1_valid__no_errors));

  // Notes on the sheet:
  //   3 ID Cost: 12XOR + 6AND + 3OR
  //   RD Cost: 12XOR + 3AND
  //   MV Cost: 5XOR gates + 1AND gate + 2OR gate
  //   Validator Cost: 7AND + 1OR + 8NOT
  //   Total: 29XOR + 17AND + 6OR + 8NOT
  //   8Bit PopCouter + 1OR
  //   m'0
  //   m'1
  //   m'2
  //   m'3
endmodule
