// Digital circuit Validit_error_display.dig as structural Verilog
module Validit_error_display (
  input  m_3d,
  input  m_3c,
  input  m_3b,
  input  m_3a,
  output _2_Errors,
  output _1_Error,
  output Valid__No_Errors
);

  wire and_1_out, and_2_out, and_3_out, and_5_out, and_6_out, not_1_out, not_2_out, not_3_out, not_4_out,
       not_5_out, not_6_out, not_7_out, not_8_out;

  not not_1 (not_1_out, m_3c);
  not not_2 (not_2_out, m_3b);
  not not_3 (not_3_out, m_3b);
  and and_1 (and_1_out, not_1_out, not_2_out);
  and and_2 (and_2_out, m_3c, m_3d);
  and and_3 (and_3_out, not_3_out, m_3d);
  and and_4 (Valid__No_Errors, not_4_out, and_1_out);
  not not_4 (not_4_out, m_3d);
  and and_5 (and_5_out, not_5_out, and_2_out);
  not not_5 (not_5_out, m_3a);
  and and_6 (and_6_out, not_6_out, and_3_out);
  not not_6 (not_6_out, m_3a);
  or or_1 (_1_Error, and_5_out, and_6_out);
  not not_7 (not_7_out, _1_Error);
  not not_8 (not_8_out, Valid__No_Errors);
  and and_7 (_2_Errors, not_7_out, not_8_out);
endmodule
